// Logisim project 1801042004.circ as structural Verilog: 10 circuits, main circuit main
module main (
  input  [31:0] Most_significant_32_bit,
  input  [31:0] Least_significant_32_bit
);

  wire a_out, b_out, c_out, clock_1_out, controlunit_1_clear, controlunit_1_compare, controlunit_1_count_m,
       controlunit_1_count_r, controlunit_1_count_u, controlunit_1_lw, controlunit_1_write_en, d_out,
       datapath_1_lose, datapath_1_match, datapath_1_win, datapath_1_writetty, e_out, f_out, g_out, h_out,
       i_out, j_out, k_out, l_out, m_out, n_out, o_out, p_out, priority_encoder_1_gs, q_out, r_out,
       Restart_out, s_out, Start_out, t_out, u_out, v_out, w_out, x_out, y_out, z_out;
  wire [2:0] controlunit_1_mux_bits;
  wire [3:0] datapath_1_ledmatrix;
  wire [4:0] priority_encoder_1_out;
  wire [6:0] datapath_1_machinescore, datapath_1_numberofch, datapath_1_ttych, datapath_1_userscore;
  wire [24:0] multiplexer_1_out;

  Button Restart (.out(Restart_out));
  Button Start (.out(Start_out));
  Button a (.out(a_out));
  Button b (.out(b_out));
  Button c (.out(c_out));
  Button d (.out(d_out));
  Button e (.out(e_out));
  Button f (.out(f_out));
  Button g (.out(g_out));
  Button h (.out(h_out));
  Button i (.out(i_out));
  Button j (.out(j_out));
  Button k (.out(k_out));
  Button l (.out(l_out));
  Button m (.out(m_out));
  Button n (.out(n_out));
  Button o (.out(o_out));
  Button p (.out(p_out));
  Button q (.out(q_out));
  Button r (.out(r_out));
  Button s (.out(s_out));
  Button t (.out(t_out));
  Button u (.out(u_out));
  Button v (.out(v_out));
  Button w (.out(w_out));
  Button x (.out(x_out));
  Button y (.out(y_out));
  Button z (.out(z_out));
  Clock clock_1 (.out(clock_1_out));
  Priority_Encoder #(.select(5)) priority_encoder_1 (
    .in0(1'b0), .in1(a_out), .in2(b_out), .in3(c_out), .in4(d_out), .in5(e_out), .in6(f_out), .in7(g_out),
    .in8(h_out), .in9(i_out), .in10(j_out), .in11(k_out), .in12(l_out), .in13(m_out), .in14(n_out),
    .in15(o_out), .in16(p_out), .in17(q_out), .in18(r_out), .in19(s_out), .in20(t_out), .in21(u_out),
    .in22(v_out), .in23(w_out), .in24(x_out), .in25(y_out), .in26(z_out), .in27(1'b0), .in28(1'b0),
    .in29(1'b0), .in30(1'b0), .in31(1'b0), .out(priority_encoder_1_out), .gs(priority_encoder_1_gs),
    .en_in(1'b1));  // open: en_out
  ControlUnit controlunit_1 (
    .restart(Restart_out), .S(Start_out), .M(datapath_1_match), .L(datapath_1_lose),
    .P(priority_encoder_1_gs), .W(datapath_1_win), .clock(clock_1_out), .write_en(controlunit_1_write_en),
    .count_R(controlunit_1_count_r), .lw(controlunit_1_lw), .count_M(controlunit_1_count_m),
    .mux_bits(controlunit_1_mux_bits), .compare(controlunit_1_compare), .count_U(controlunit_1_count_u),
    .clear(controlunit_1_clear));
  DataPath datapath_1 (
    .Load_Word(controlunit_1_lw), .Most_significant_32_bit(Most_significant_32_bit),
    .Least_significant_32_bit(Least_significant_32_bit), .chi(priority_encoder_1_out),
    .lchi(priority_encoder_1_gs), .write_en(controlunit_1_write_en), .mux_bits(controlunit_1_mux_bits),
    .count_R(controlunit_1_count_r), .clock(clock_1_out), .compare(controlunit_1_compare),
    .count_M(controlunit_1_count_m), .count_U(controlunit_1_count_u), .restart(Restart_out),
    .NumberOfch(datapath_1_numberofch), .Lose(datapath_1_lose), .Win(datapath_1_win),
    .match(datapath_1_match), .TTYch(datapath_1_ttych), .WriteTTY(datapath_1_writetty),
    .MachineScore(datapath_1_machinescore), .UserScore(datapath_1_userscore), .LedMatrix(datapath_1_ledmatrix));
  Multiplexer #(.select(4), .width(25), .enable("false")) multiplexer_1 (
    .in0({25{1'b0}}), .in1(25'h1f00000), .in2(25'h1f84000), .in3(25'h1f84210), .in4(25'h1f84310),
    .in5(25'h1f84390), .in6(25'h1f85390), .in7(25'h1f85394), .in8(25'h1f853d4), .in9(25'h1f857d4),
    .in10(25'h1f857d5), .out(multiplexer_1_out), .sel(datapath_1_ledmatrix));  // open: in11, in12, in13, in14, in15
  TTY tty_1 (.data(datapath_1_ttych), .clk(clock_1_out), .we(datapath_1_writetty), .clr(controlunit_1_clear));
  DotMatrix #(.matrixrows(5)) dotmatrix_1 (
    .col0(multiplexer_1_out[24:20]), .col1(multiplexer_1_out[19:15]), .col2(multiplexer_1_out[14:10]),
    .col3(multiplexer_1_out[9:5]), .col4(multiplexer_1_out[4:0]));
  _7_Segment_Display u_7_segment_display_1 (
    .g(datapath_1_numberofch[6]), .f(datapath_1_numberofch[5]), .a(datapath_1_numberofch[0]),
    .b(datapath_1_numberofch[1]), .e(datapath_1_numberofch[4]), .d(datapath_1_numberofch[3]),
    .c(datapath_1_numberofch[2]));  // open: dp
  _7_Segment_Display u_7_segment_display_2 (
    .g(datapath_1_machinescore[6]), .f(datapath_1_machinescore[5]), .a(datapath_1_machinescore[0]),
    .b(datapath_1_machinescore[1]), .e(datapath_1_machinescore[4]), .d(datapath_1_machinescore[3]),
    .c(datapath_1_machinescore[2]));  // open: dp
  _7_Segment_Display u_7_segment_display_3 (
    .g(datapath_1_userscore[6]), .f(datapath_1_userscore[5]), .a(datapath_1_userscore[0]),
    .b(datapath_1_userscore[1]), .e(datapath_1_userscore[4]), .d(datapath_1_userscore[3]),
    .c(datapath_1_userscore[2]));  // open: dp

  // Notes on the sheet:
  //   number of characters
  //   machine score
  //   user score
endmodule

module NumberOfCharacters (
  input  c7,
  input  c6,
  input  c5,
  input  c4,
  input  c3,
  input  c2,
  input  c1,
  input  c0,
  output n3,
  output n2,
  output n1,
  output n0
);

  wire and_2_out, and_3_out, and_4_out, and_5_out, and_6_out, and_7_out, not_1_out, not_2_out, not_3_out,
       not_4_out, not_5_out, not_6_out, not_7_out;

  not not_1 (not_1_out, c7);
  not not_2 (not_2_out, c3);
  not not_3 (not_3_out, c7);
  not not_4 (not_4_out, c1);
  not not_5 (not_5_out, c3);
  not not_6 (not_6_out, c5);
  not not_7 (not_7_out, c7);
  and and_1 (n2, not_1_out, c3);
  and and_2 (and_2_out, not_2_out, c1);
  and and_3 (and_3_out, not_3_out, c5);
  and and_4 (and_4_out, not_4_out, c0);
  and and_5 (and_5_out, not_5_out, c2);
  and and_6 (and_6_out, not_6_out, c4);
  and and_7 (and_7_out, not_7_out, c6);
  or or_1 (n1, and_2_out, and_3_out);
  or or_2 (n0, and_4_out, and_5_out, and_6_out, and_7_out);

  assign n3 = c7;
endmodule

module BCDto7_SegmentDecoder (
  input  A,
  input  B,
  input  C,
  input  D,
  output a_2,
  output b_2,
  output c_2,
  output d_2,
  output e,
  output f,
  output g
);

  wire and_1_out, and_2_out, and_3_out, and_4_out, and_5_out, and_6_out, and_7_out, and_8_out, and_9_out,
       not_1_out, not_2_out, not_3_out;

  not not_1 (not_1_out, B);
  not not_2 (not_2_out, C);
  not not_3 (not_3_out, D);
  and and_1 (and_1_out, not_1_out, not_3_out);
  and and_2 (and_2_out, B, D);
  and and_3 (and_3_out, B, not_3_out);
  and and_4 (and_4_out, C, D);
  and and_5 (and_5_out, not_2_out, not_3_out);
  and and_6 (and_6_out, C, not_3_out);
  and and_7 (and_7_out, B, not_2_out, D);
  and and_8 (and_8_out, not_1_out, C);
  and and_9 (and_9_out, B, not_2_out);
  or or_1 (a_2, A, and_1_out, and_2_out, C);
  or or_2 (b_2, not_1_out, and_4_out, and_5_out);
  or or_3 (c_2, B, D, and_5_out);
  or or_4 (d_2, A, and_1_out, and_6_out, and_7_out, and_8_out);
  or or_5 (e, and_1_out, and_6_out);
  or or_6 (f, A, and_3_out, and_5_out, and_9_out);
  or or_7 (g, A, and_8_out, and_6_out, and_9_out);
endmodule

module MyComparator (
  input  [7:0] chi,
  input  [7:0] ch0,
  output equal
);

  wire [7:0] xnor_1_out;

  assign xnor_1_out = ~(chi ^ ch0);  // XNOR_Gate xnor_1, 8 bits wide
  and and_1 (equal, xnor_1_out[0], xnor_1_out[1], xnor_1_out[2], xnor_1_out[3], xnor_1_out[4], xnor_1_out[5], xnor_1_out[6], xnor_1_out[7]);
endmodule

module CompareWithWord (
  input  compare,
  input  [7:0] chi,
  input  [7:0] ch0,
  input  [7:0] ch1,
  input  [7:0] ch2,
  input  [7:0] ch3,
  input  [7:0] ch4,
  input  [7:0] ch5,
  input  [7:0] ch6,
  input  [7:0] ch7,
  output [7:0] isFound,
  output match
);

  wire mycomparator_1_equal, mycomparator_2_equal, mycomparator_3_equal, mycomparator_4_equal,
       mycomparator_5_equal, mycomparator_6_equal, mycomparator_7_equal, mycomparator_8_equal,
       mycomparator_9_equal, mycomparator_10_equal, mycomparator_11_equal, mycomparator_12_equal,
       mycomparator_13_equal, mycomparator_14_equal, mycomparator_15_equal, mycomparator_16_equal;
  wire [7:0] or_2_out;

  MyComparator mycomparator_1 (.chi(chi), .ch0(ch0), .equal(mycomparator_1_equal));
  MyComparator mycomparator_2 (.chi(chi), .ch0(ch1), .equal(mycomparator_2_equal));
  MyComparator mycomparator_3 (.chi(chi), .ch0(ch2), .equal(mycomparator_3_equal));
  MyComparator mycomparator_4 (.chi(chi), .ch0(ch3), .equal(mycomparator_4_equal));
  MyComparator mycomparator_5 (.chi(chi), .ch0(ch4), .equal(mycomparator_5_equal));
  MyComparator mycomparator_6 (.chi(chi), .ch0(ch5), .equal(mycomparator_6_equal));
  MyComparator mycomparator_7 (.chi(chi), .ch0(ch6), .equal(mycomparator_7_equal));
  MyComparator mycomparator_8 (.chi(chi), .ch0(ch7), .equal(mycomparator_8_equal));
  MyComparator mycomparator_9 (.chi({8{1'b0}}), .ch0(ch0), .equal(mycomparator_9_equal));
  MyComparator mycomparator_10 (.chi({8{1'b0}}), .ch0(ch1), .equal(mycomparator_10_equal));
  MyComparator mycomparator_11 (.chi({8{1'b0}}), .ch0(ch2), .equal(mycomparator_11_equal));
  MyComparator mycomparator_12 (.chi({8{1'b0}}), .ch0(ch3), .equal(mycomparator_12_equal));
  MyComparator mycomparator_13 (.chi({8{1'b0}}), .ch0(ch4), .equal(mycomparator_13_equal));
  MyComparator mycomparator_14 (.chi({8{1'b0}}), .ch0(ch5), .equal(mycomparator_14_equal));
  MyComparator mycomparator_15 (.chi({8{1'b0}}), .ch0(ch6), .equal(mycomparator_15_equal));
  MyComparator mycomparator_16 (.chi({8{1'b0}}), .ch0(ch7), .equal(mycomparator_16_equal));
  or or_1 (match, mycomparator_1_equal, mycomparator_2_equal, mycomparator_3_equal, mycomparator_4_equal, mycomparator_5_equal, mycomparator_6_equal, mycomparator_7_equal, mycomparator_8_equal);
  or or_2 (or_2_out[0], mycomparator_1_equal, mycomparator_9_equal);
  or or_3 (or_2_out[1], mycomparator_2_equal, mycomparator_10_equal);
  or or_4 (or_2_out[2], mycomparator_3_equal, mycomparator_11_equal);
  or or_5 (or_2_out[3], mycomparator_4_equal, mycomparator_12_equal);
  or or_6 (or_2_out[4], mycomparator_5_equal, mycomparator_13_equal);
  or or_7 (or_2_out[5], mycomparator_6_equal, mycomparator_14_equal);
  or or_8 (or_2_out[6], mycomparator_7_equal, mycomparator_15_equal);
  or or_9 (or_2_out[7], mycomparator_8_equal, mycomparator_16_equal);
  Multiplexer #(.width(8), .enable("false")) multiplexer_1 (
    .in0({8{1'b0}}), .in1(or_2_out), .out(isFound), .sel(compare));
endmodule

module IsFoundRegisters (
  input  [7:0] isFound__D,
  input  Reset,
  input  clock,
  output [7:0] isFound__Q,
  output Founded
);

  Register #(.width(1)) ch0 (.D(isFound__D[0]), .en(isFound__D[0]), .Q(isFound__Q[0]), .clk(clock), .clr(Reset));
  Register #(.width(1)) ch1 (.D(isFound__D[1]), .en(isFound__D[1]), .Q(isFound__Q[1]), .clk(clock), .clr(Reset));
  Register #(.width(1)) ch2 (.D(isFound__D[2]), .en(isFound__D[2]), .Q(isFound__Q[2]), .clk(clock), .clr(Reset));
  Register #(.width(1)) ch3 (.D(isFound__D[3]), .en(isFound__D[3]), .Q(isFound__Q[3]), .clk(clock), .clr(Reset));
  Register #(.width(1)) ch4 (.D(isFound__D[4]), .en(isFound__D[4]), .Q(isFound__Q[4]), .clk(clock), .clr(Reset));
  Register #(.width(1)) ch5 (.D(isFound__D[5]), .en(isFound__D[5]), .Q(isFound__Q[5]), .clk(clock), .clr(Reset));
  Register #(.width(1)) ch6 (.D(isFound__D[6]), .en(isFound__D[6]), .Q(isFound__Q[6]), .clk(clock), .clr(Reset));
  Register #(.width(1)) ch7 (.D(isFound__D[7]), .en(isFound__D[7]), .Q(isFound__Q[7]), .clk(clock), .clr(Reset));
  and and_1 (Founded, isFound__Q[0], isFound__Q[1], isFound__Q[2], isFound__Q[3], isFound__Q[4], isFound__Q[5], isFound__Q[6], isFound__Q[7]);
endmodule

module DataPath (
  input  restart,
  input  Load_Word,
  input  [31:0] Most_significant_32_bit,
  input  [31:0] Least_significant_32_bit,
  input  [4:0] chi,
  input  lchi,
  input  write_en,
  input  [2:0] mux_bits,
  input  count_R,
  input  clock,
  input  compare,
  input  count_M,
  input  count_U,
  output [6:0] NumberOfch,
  output Lose,
  output Win,
  output match,
  output [6:0] TTYch,
  output WriteTTY,
  output [6:0] MachineScore,
  output [6:0] UserScore,
  output [3:0] LedMatrix
);

  wire comparator_1_gt, displayontty_1_valid, numberofcharacters_1_n0, numberofcharacters_1_n1,
       numberofcharacters_1_n2, numberofcharacters_1_n3, synchronizer_1_bo, synchronizer_2_bo;
  wire [3:0] machine_q, user_q;
  wire [7:0] ch0_q, ch1_q, ch2_q, ch3_q, ch4_q, ch5_q, ch6_q, ch7_q, comparewithword_1_isfound,
       isfoundregisters_1_isfound__q, register_1_q;

  Register ch7 (.D(Most_significant_32_bit[31:24]), .en(Load_Word), .Q(ch7_q), .clk(clock), .clr(restart));
  Register ch6 (.D(Most_significant_32_bit[23:16]), .en(Load_Word), .Q(ch6_q), .clk(clock), .clr(restart));
  Register ch5 (.D(Most_significant_32_bit[15:8]), .en(Load_Word), .Q(ch5_q), .clk(clock), .clr(restart));
  Register ch4 (.D(Most_significant_32_bit[7:0]), .en(Load_Word), .Q(ch4_q), .clk(clock), .clr(restart));
  Register ch3 (.D(Least_significant_32_bit[31:24]), .en(Load_Word), .Q(ch3_q), .clk(clock), .clr(restart));
  Register ch2 (.D(Least_significant_32_bit[23:16]), .en(Load_Word), .Q(ch2_q), .clk(clock), .clr(restart));
  Register ch1 (.D(Least_significant_32_bit[15:8]), .en(Load_Word), .Q(ch1_q), .clk(clock), .clr(restart));
  Register ch0 (.D(Least_significant_32_bit[7:0]), .en(Load_Word), .Q(ch0_q), .clk(clock), .clr(restart));
  Register register_1 (.D({3'b011, chi}), .en(lchi), .Q(register_1_q), .clk(clock), .clr(restart));
  CompareWithWord comparewithword_1 (
    .compare(compare), .chi(register_1_q), .ch0(ch0_q), .ch1(ch1_q), .ch2(ch2_q), .ch3(ch3_q), .ch4(ch4_q),
    .ch5(ch5_q), .ch6(ch6_q), .ch7(ch7_q), .isFound(comparewithword_1_isfound), .match(match));
  NumberOfCharacters numberofcharacters_1 (
    .c7(ch7_q[6]), .c6(ch6_q[6]), .c5(ch5_q[6]), .c4(ch4_q[6]), .c3(ch3_q[6]), .c2(ch2_q[6]), .c1(ch1_q[6]),
    .c0(ch0_q[6]), .n3(numberofcharacters_1_n3), .n2(numberofcharacters_1_n2), .n1(numberofcharacters_1_n1),
    .n0(numberofcharacters_1_n0));
  BCDto7_SegmentDecoder bcdto7_segmentdecoder_1 (
    .A(numberofcharacters_1_n3), .B(numberofcharacters_1_n2), .C(numberofcharacters_1_n1),
    .D(numberofcharacters_1_n0), .a_2(NumberOfch[0]), .b_2(NumberOfch[1]), .c_2(NumberOfch[2]),
    .d_2(NumberOfch[3]), .e(NumberOfch[4]), .f(NumberOfch[5]), .g(NumberOfch[6]));
  IsFoundRegisters isfoundregisters_1 (
    .isFound__D(comparewithword_1_isfound), .Reset(restart), .clock(clock),
    .isFound__Q(isfoundregisters_1_isfound__q), .Founded(Win));
  DisplayOnTTY displayontty_1 (
    .ch0(ch0_q), .ch1(ch1_q), .ch2(ch2_q), .ch3(ch3_q), .ch4(ch4_q), .ch5(ch5_q), .ch6(ch6_q), .ch7(ch7_q),
    .isFound(isfoundregisters_1_isfound__q), .mux_bits(mux_bits), .lose(Lose), .TTYch(TTYch),
    .valid(displayontty_1_valid));
  Counter #(.width(4), .max('hf)) trial (
    .count(count_R), .Q(LedMatrix), .clk(clock), .clr(restart));  // open: load, D, carry
  synchronizer synchronizer_1 (.bi(count_M), .Clock(clock), .bo(synchronizer_1_bo));
  not not_1 (Lose, comparator_1_gt);
  Comparator #(.width(4), .mode("unsigned")) comparator_1 (
    .a(4'b1010), .b(LedMatrix), .gt(comparator_1_gt));  // open: eq, lt
  Counter #(.width(4), .max('hf)) machine (
    .count(synchronizer_1_bo), .Q(machine_q), .clk(clock));  // open: load, D, carry, clr
  synchronizer synchronizer_2 (.bi(count_U), .Clock(clock), .bo(synchronizer_2_bo));
  Counter #(.width(4), .max('hf)) user (
    .count(synchronizer_2_bo), .Q(user_q), .clk(clock));  // open: load, D, carry, clr
  and and_1 (WriteTTY, displayontty_1_valid, write_en);
  BCDto7_SegmentDecoder bcdto7_segmentdecoder_2 (
    .A(machine_q[3]), .B(machine_q[2]), .C(machine_q[1]), .D(machine_q[0]), .a_2(MachineScore[0]),
    .b_2(MachineScore[1]), .c_2(MachineScore[2]), .d_2(MachineScore[3]), .e(MachineScore[4]),
    .f(MachineScore[5]), .g(MachineScore[6]));
  BCDto7_SegmentDecoder bcdto7_segmentdecoder_3 (
    .A(user_q[3]), .B(user_q[2]), .C(user_q[1]), .D(user_q[0]), .a_2(UserScore[0]), .b_2(UserScore[1]),
    .c_2(UserScore[2]), .d_2(UserScore[3]), .e(UserScore[4]), .f(UserScore[5]), .g(UserScore[6]));
endmodule

module ControlUnit (
  input  restart,
  input  S,
  input  M,
  input  clock,
  input  L,
  input  P,
  input  W,
  output write_en,
  output count_R,
  output lw,
  output count_M,
  output [2:0] mux_bits,
  output compare,
  output count_U,
  output clear
);

  wire and_1_out, and_2_out, and_3_out, and_4_out, and_5_out, and_6_out, and_7_out, and_8_out, and_12_out,
       and_13_out, and_14_out, and_15_out, and_16_out, and_17_out, and_18_out, and_19_out, and_20_out,
       and_21_out, and_22_out, and_23_out, and_24_out, and_25_out, and_26_out, and_27_out, and_28_out,
       and_29_out, and_30_out, and_31_out, and_32_out, and_33_out, and_34_out, and_35_out, and_36_out,
       and_37_out, and_38_out, and_39_out, and_40_out, and_41_out, and_42_out, and_43_out, and_44_out,
       and_45_out, and_46_out, and_47_out, and_48_out, and_49_out, and_50_out, and_53_out, and_54_out,
       not_1_out, not_2_out, not_3_out, not_4_out, not_5_out, not_6_out, not_7_out, not_8_out, not_9_out,
       not_10_out, not_11_out, not_12_out, not_13_out, not_14_out, not_15_out, not_16_out, not_17_out,
       not_18_out, not_19_out, not_20_out, not_21_out, not_22_out, not_23_out, not_24_out, not_25_out,
       not_26_out, not_27_out, not_28_out, not_29_out, not_30_out, not_31_out, not_32_out, not_33_out,
       not_34_out, not_35_out, not_36_out, not_37_out, not_38_out, not_39_out, not_40_out, not_41_out,
       not_42_out, not_43_out, not_44_out, not_45_out, not_46_out, not_47_out, not_48_out, not_49_out,
       not_50_out, not_51_out, not_52_out, not_53_out, not_54_out, not_55_out, not_56_out, not_57_out,
       not_58_out, not_59_out, not_60_out, not_61_out, not_62_out, not_63_out, not_64_out, not_65_out,
       not_66_out, not_67_out, not_68_out, not_69_out, not_70_out, not_71_out, not_72_out, not_73_out,
       not_74_out, not_75_out, not_76_out, not_77_out, not_78_out, not_79_out, not_80_out, not_81_out,
       not_82_out, not_83_out, not_84_out, not_85_out, not_86_out, not_87_out, not_88_out, not_89_out,
       not_90_out, not_91_out, not_92_out, not_93_out, not_94_out, not_95_out, not_96_out, not_97_out,
       not_98_out, not_99_out, not_100_out, not_101_out, not_102_out, not_103_out, not_104_out, not_105_out,
       not_106_out, not_107_out, not_108_out, not_109_out, not_110_out, not_111_out, not_112_out,
       not_113_out, not_114_out, not_115_out, not_116_out, not_117_out, not_118_out, not_119_out, not_120_out;
  wire [3:0] or_8_out, STATES_q;

  not not_1 (not_1_out, STATES_q[3]);
  not not_2 (not_2_out, STATES_q[2]);
  not not_3 (not_3_out, STATES_q[1]);
  not not_4 (not_4_out, STATES_q[0]);
  not not_5 (not_5_out, STATES_q[2]);
  not not_6 (not_6_out, STATES_q[1]);
  not not_7 (not_7_out, STATES_q[2]);
  not not_8 (not_8_out, STATES_q[0]);
  not not_9 (not_9_out, STATES_q[2]);
  not not_10 (not_10_out, STATES_q[1]);
  not not_11 (not_11_out, STATES_q[0]);
  not not_12 (not_12_out, STATES_q[1]);
  not not_13 (not_13_out, STATES_q[3]);
  not not_14 (not_14_out, STATES_q[2]);
  not not_15 (not_15_out, STATES_q[0]);
  not not_16 (not_16_out, L);
  not not_17 (not_17_out, W);
  not not_18 (not_18_out, STATES_q[3]);
  not not_19 (not_19_out, STATES_q[2]);
  not not_20 (not_20_out, STATES_q[0]);
  not not_21 (not_21_out, L);
  not not_22 (not_22_out, P);
  not not_23 (not_23_out, W);
  not not_24 (not_24_out, STATES_q[3]);
  not not_25 (not_25_out, STATES_q[2]);
  not not_26 (not_26_out, STATES_q[0]);
  not not_27 (not_27_out, W);
  not not_28 (not_28_out, STATES_q[3]);
  not not_29 (not_29_out, STATES_q[2]);
  not not_30 (not_30_out, STATES_q[0]);
  not not_31 (not_31_out, W);
  not not_32 (not_32_out, STATES_q[3]);
  not not_33 (not_33_out, STATES_q[2]);
  not not_34 (not_34_out, STATES_q[0]);
  not not_35 (not_35_out, L);
  not not_36 (not_36_out, W);
  not not_37 (not_37_out, STATES_q[3]);
  not not_38 (not_38_out, STATES_q[3]);
  not not_39 (not_39_out, STATES_q[0]);
  not not_40 (not_40_out, STATES_q[3]);
  not not_41 (not_41_out, STATES_q[2]);
  not not_42 (not_42_out, STATES_q[1]);
  not not_43 (not_43_out, STATES_q[3]);
  not not_44 (not_44_out, STATES_q[2]);
  not not_45 (not_45_out, STATES_q[2]);
  not not_46 (not_46_out, STATES_q[1]);
  not not_47 (not_47_out, STATES_q[0]);
  not not_48 (not_48_out, STATES_q[1]);
  not not_49 (not_49_out, STATES_q[0]);
  not not_50 (not_50_out, STATES_q[2]);
  not not_51 (not_51_out, STATES_q[1]);
  not not_52 (not_52_out, STATES_q[2]);
  not not_53 (not_53_out, STATES_q[0]);
  not not_54 (not_54_out, STATES_q[1]);
  not not_55 (not_55_out, STATES_q[0]);
  not not_56 (not_56_out, STATES_q[2]);
  not not_57 (not_57_out, STATES_q[1]);
  not not_58 (not_58_out, STATES_q[0]);
  not not_59 (not_59_out, STATES_q[2]);
  not not_60 (not_60_out, STATES_q[0]);
  not not_61 (not_61_out, STATES_q[1]);
  not not_62 (not_62_out, STATES_q[0]);
  not not_63 (not_63_out, STATES_q[0]);
  and and_1 (and_1_out, not_1_out, STATES_q[2], STATES_q[1], STATES_q[0]);
  and and_2 (and_2_out, STATES_q[3], not_2_out, not_3_out, not_4_out);
  and and_3 (and_3_out, STATES_q[3], not_5_out, not_6_out, STATES_q[0]);
  and and_4 (and_4_out, STATES_q[3], not_7_out, STATES_q[1], not_8_out);
  and and_5 (and_5_out, STATES_q[3], not_9_out, STATES_q[1], STATES_q[0]);
  and and_6 (and_6_out, STATES_q[3], STATES_q[2], not_10_out, not_11_out);
  and and_7 (and_7_out, STATES_q[3], STATES_q[2], not_12_out, STATES_q[0]);
  not not_64 (not_64_out, STATES_q[3]);
  not not_65 (not_65_out, STATES_q[2]);
  not not_66 (not_66_out, STATES_q[0]);
  not not_67 (not_67_out, STATES_q[3]);
  not not_68 (not_68_out, STATES_q[1]);
  not not_69 (not_69_out, STATES_q[0]);
  not not_70 (not_70_out, STATES_q[3]);
  not not_71 (not_71_out, STATES_q[1]);
  not not_72 (not_72_out, STATES_q[3]);
  not not_73 (not_73_out, STATES_q[0]);
  not not_74 (not_74_out, STATES_q[2]);
  not not_75 (not_75_out, STATES_q[1]);
  not not_76 (not_76_out, STATES_q[0]);
  not not_77 (not_77_out, STATES_q[1]);
  not not_78 (not_78_out, STATES_q[3]);
  not not_79 (not_79_out, STATES_q[2]);
  not not_80 (not_80_out, STATES_q[1]);
  not not_81 (not_81_out, STATES_q[3]);
  not not_82 (not_82_out, STATES_q[2]);
  not not_83 (not_83_out, STATES_q[3]);
  not not_84 (not_84_out, STATES_q[1]);
  not not_85 (not_85_out, STATES_q[3]);
  not not_86 (not_86_out, STATES_q[0]);
  not not_87 (not_87_out, STATES_q[2]);
  not not_88 (not_88_out, STATES_q[1]);
  not not_89 (not_89_out, STATES_q[2]);
  not not_90 (not_90_out, STATES_q[0]);
  not not_91 (not_91_out, STATES_q[1]);
  not not_92 (not_92_out, STATES_q[0]);
  not not_93 (not_93_out, STATES_q[3]);
  not not_94 (not_94_out, STATES_q[2]);
  not not_95 (not_95_out, STATES_q[1]);
  not not_96 (not_96_out, STATES_q[0]);
  not not_97 (not_97_out, STATES_q[3]);
  not not_98 (not_98_out, STATES_q[2]);
  not not_99 (not_99_out, STATES_q[3]);
  not not_100 (not_100_out, STATES_q[1]);
  not not_101 (not_101_out, STATES_q[3]);
  not not_102 (not_102_out, STATES_q[0]);
  not not_103 (not_103_out, STATES_q[2]);
  not not_104 (not_104_out, STATES_q[1]);
  not not_105 (not_105_out, STATES_q[0]);
  not not_106 (not_106_out, STATES_q[2]);
  not not_107 (not_107_out, STATES_q[0]);
  not not_108 (not_108_out, STATES_q[1]);
  not not_109 (not_109_out, STATES_q[0]);
  and and_8 (and_8_out, not_37_out, STATES_q[2], STATES_q[1], STATES_q[0]);
  and and_9 (count_R, not_38_out, STATES_q[2], STATES_q[1], not_39_out);
  and and_10 (lw, not_40_out, not_41_out, not_42_out, STATES_q[0]);
  and and_11 (count_M, not_43_out, not_44_out, STATES_q[1], STATES_q[0]);
  and and_12 (and_12_out, STATES_q[3], not_45_out, STATES_q[1], STATES_q[0]);
  and and_13 (and_13_out, STATES_q[3], STATES_q[2], not_46_out, not_47_out);
  and and_14 (and_14_out, STATES_q[3], STATES_q[2], not_48_out, STATES_q[0]);
  and and_15 (and_15_out, STATES_q[3], STATES_q[2], STATES_q[1], not_49_out);
  and and_16 (and_16_out, STATES_q[3], not_50_out, not_51_out, STATES_q[0]);
  and and_17 (and_17_out, STATES_q[3], not_52_out, STATES_q[1], not_53_out);
  and and_18 (and_18_out, STATES_q[3], STATES_q[2], not_54_out, STATES_q[0]);
  and and_19 (and_19_out, STATES_q[3], STATES_q[2], STATES_q[1], not_55_out);
  and and_20 (and_20_out, STATES_q[3], not_56_out, not_57_out, not_58_out);
  and and_21 (and_21_out, STATES_q[3], not_59_out, STATES_q[1], not_60_out);
  and and_22 (and_22_out, STATES_q[3], STATES_q[2], not_61_out, not_62_out);
  and and_23 (and_23_out, STATES_q[3], STATES_q[2], STATES_q[1], not_63_out);
  not not_110 (not_110_out, STATES_q[3]);
  not not_111 (not_111_out, STATES_q[1]);
  not not_112 (not_112_out, STATES_q[3]);
  not not_113 (not_113_out, STATES_q[1]);
  not not_114 (not_114_out, STATES_q[0]);
  not not_115 (not_115_out, STATES_q[3]);
  not not_116 (not_116_out, STATES_q[1]);
  not not_117 (not_117_out, STATES_q[3]);
  not not_118 (not_118_out, STATES_q[2]);
  not not_119 (not_119_out, STATES_q[1]);
  not not_120 (not_120_out, STATES_q[0]);
  and and_24 (and_24_out, not_64_out, not_65_out, STATES_q[1], not_66_out, W);
  and and_25 (and_25_out, not_13_out, not_14_out, STATES_q[1], not_15_out, not_16_out, P, not_17_out);
  and and_26 (and_26_out, not_67_out, STATES_q[2], not_68_out, not_69_out);
  and and_27 (and_27_out, not_70_out, STATES_q[2], not_71_out, STATES_q[0]);
  and and_28 (and_28_out, not_72_out, STATES_q[2], STATES_q[1], not_73_out);
  and and_29 (and_29_out, STATES_q[3], not_74_out, STATES_q[1], STATES_q[0]);
  and and_30 (and_30_out, STATES_q[3], STATES_q[2], not_75_out, not_76_out);
  and and_31 (and_31_out, STATES_q[3], STATES_q[2], not_77_out, STATES_q[0]);
  and and_32 (and_32_out, not_78_out, not_79_out, not_80_out, STATES_q[0]);
  and and_33 (and_33_out, not_18_out, not_19_out, STATES_q[1], not_20_out, not_21_out, not_22_out, not_23_out);
  and and_34 (and_34_out, not_24_out, not_25_out, STATES_q[1], not_26_out, L, not_27_out);
  and and_35 (and_35_out, not_81_out, not_82_out, STATES_q[1], STATES_q[0]);
  and and_36 (and_36_out, not_83_out, STATES_q[2], not_84_out, STATES_q[0]);
  and and_37 (and_37_out, not_85_out, STATES_q[2], STATES_q[1], not_86_out);
  and and_38 (and_38_out, STATES_q[3], not_87_out, not_88_out, STATES_q[0]);
  and and_39 (and_39_out, STATES_q[3], not_89_out, STATES_q[1], not_90_out);
  and and_40 (and_40_out, STATES_q[3], STATES_q[2], not_91_out, STATES_q[0]);
  and and_41 (and_41_out, STATES_q[3], STATES_q[2], STATES_q[1], not_92_out);
  and and_42 (and_42_out, not_93_out, not_94_out, not_95_out, not_96_out, S);
  and and_43 (and_43_out, not_28_out, not_29_out, STATES_q[1], not_30_out, L, not_31_out);
  and and_44 (and_44_out, not_32_out, not_33_out, STATES_q[1], not_34_out, not_35_out, P, not_36_out);
  and and_45 (and_45_out, not_97_out, not_98_out, STATES_q[1], STATES_q[0]);
  and and_46 (and_46_out, not_99_out, STATES_q[2], not_100_out, STATES_q[0], M);
  and and_47 (and_47_out, not_101_out, STATES_q[2], STATES_q[1], not_102_out);
  and and_48 (and_48_out, STATES_q[3], not_103_out, not_104_out, not_105_out);
  and and_49 (and_49_out, STATES_q[3], not_106_out, STATES_q[1], not_107_out);
  and and_50 (and_50_out, STATES_q[3], STATES_q[2], not_108_out, not_109_out);
  or or_1 (write_en, STATES_q[3], and_8_out);
  or or_2 (mux_bits[2], and_12_out, and_13_out, and_14_out, and_15_out);
  or or_3 (mux_bits[1], and_16_out, and_17_out, and_18_out, and_19_out);
  or or_4 (mux_bits[0], and_20_out, and_21_out, and_22_out, and_23_out);
  and and_51 (compare, not_110_out, STATES_q[2], not_111_out, STATES_q[0]);
  and and_52 (count_U, not_112_out, STATES_q[2], not_113_out, not_114_out);
  and and_53 (and_53_out, not_115_out, STATES_q[2], not_116_out, STATES_q[0]);
  and and_54 (and_54_out, not_117_out, not_118_out, not_119_out, not_120_out);
  or or_5 (or_8_out[3], and_1_out, and_2_out, and_3_out, and_4_out, and_5_out, and_6_out, and_7_out);
  or or_6 (or_8_out[2], and_24_out, and_25_out, and_26_out, and_27_out, and_28_out, and_29_out, and_30_out, and_31_out);
  or or_7 (or_8_out[1], and_32_out, and_33_out, and_34_out, and_35_out, and_36_out, and_37_out, and_38_out, and_39_out, and_40_out, and_41_out);
  or or_8 (or_8_out[0], and_42_out, and_43_out, and_44_out, and_45_out, and_46_out, and_47_out, and_48_out, and_49_out, and_50_out);
  or or_9 (clear, and_53_out, and_54_out);
  Register #(.width(4)) STATES (.D(or_8_out), .en(1'b1), .Q(STATES_q), .clk(clock), .clr(restart));
endmodule

module DisplayOnTTY (
  input  [7:0] ch0,
  input  [7:0] ch1,
  input  [7:0] ch2,
  input  [7:0] ch3,
  input  [7:0] ch4,
  input  [7:0] ch5,
  input  [7:0] ch6,
  input  [7:0] ch7,
  input  [7:0] isFound,
  input  [2:0] mux_bits,
  input  lose,
  output [6:0] TTYch,
  output valid
);

  wire multiplexer_2_out, mycomparator_1_equal, or_1_out;
  wire [7:0] multiplexer_1_out;
  wire [7:7] multiplexer_3_out;

  Multiplexer #(.select(3), .width(8), .enable("false")) multiplexer_1 (
    .in0(ch7), .in1(ch6), .in2(ch5), .in3(ch4), .in4(ch3), .in5(ch2), .in6(ch1), .in7(ch0),
    .out(multiplexer_1_out), .sel(mux_bits));
  Multiplexer #(.select(3), .enable("false")) multiplexer_2 (
    .in0(isFound[7]), .in1(isFound[6]), .in2(isFound[5]), .in3(isFound[4]), .in4(isFound[3]),
    .in5(isFound[2]), .in6(isFound[1]), .in7(isFound[0]), .out(multiplexer_2_out), .sel(mux_bits));
  or or_1 (or_1_out, lose, multiplexer_2_out);
  Multiplexer #(.width(8), .enable("false")) multiplexer_3 (
    .in0(8'h2a), .in1(multiplexer_1_out), .out({multiplexer_3_out[7], TTYch}), .sel(or_1_out));
  MyComparator mycomparator_1 (.chi({8{1'b0}}), .ch0(multiplexer_1_out), .equal(mycomparator_1_equal));
  not not_1 (valid, mycomparator_1_equal);
endmodule

module synchronizer (
  input  bi,
  input  Clock,
  output bo
);

  wire and_1_out, and_2_out, not_1_out, not_2_out, not_3_out, not_4_out, not_5_out;
  wire [1:0] and_3_out, register_1_q;

  not not_1 (not_1_out, register_1_q[1]);
  not not_2 (not_2_out, register_1_q[0]);
  not not_3 (not_3_out, register_1_q[1]);
  not not_4 (not_4_out, register_1_q[0]);
  not not_5 (not_5_out, register_1_q[1]);
  and and_1 (and_1_out, not_1_out, register_1_q[0], bi);
  and and_2 (and_2_out, register_1_q[1], not_2_out, bi);
  and and_3 (and_3_out[0], not_3_out, not_4_out, bi);
  and and_4 (bo, not_5_out, register_1_q[0]);
  or or_1 (and_3_out[1], and_1_out, and_2_out);
  Register #(.width(2)) register_1 (.D(and_3_out), .en(1'b1), .Q(register_1_q), .clk(Clock));  // open: clr

  // Notes on the sheet:
  //   s0
  //   s1
  //   n1
  //   n0
endmodule
