// Logisim project 1801042004.circ as structural Verilog: 4 circuits, main circuit main
module main (
);

  wire BL__button_left_out, BR__button_right_out, Button_Synchronizer_2_bo, Button_Synchronizer_3_bo,
       Button_Synchronizer_4_bo, Button_Synchronizer_bo, Clock_out, Game_l1, Game_l2, Game_l3, Game_r1,
       Game_r2, Game_r3, Game_s, Reset_out, Score_Board_Reset_out;
  wire [3:0] Left_Score_Board_score, Right_Score_Board_score;

  Button BL__button_left (.out(BL__button_left_out));
  Hex_Digit_Display hex_digit_display_1 (.value(Left_Score_Board_score));  // open: dp
  score_board Left_Score_Board (
    .W(Button_Synchronizer_2_bo), .Clock(Clock_out), .Reset(Score_Board_Reset_out),
    .Score(Left_Score_Board_score));
  Button Score_Board_Reset (.out(Score_Board_Reset_out));
  button_synchronizer Button_Synchronizer (.bi(BL__button_left_out), .Clock(Clock_out), .bo(Button_Synchronizer_bo));
  button_synchronizer Button_Synchronizer_2 (.bi(Game_l3), .Clock(Clock_out), .bo(Button_Synchronizer_2_bo));
  Button Reset (.out(Reset_out));
  Turn_Leds Game (
    .BL(Button_Synchronizer_bo), .BR(Button_Synchronizer_3_bo), .Reset(Reset_out), .Clock(Clock_out),
    .L3(Game_l3), .L2(Game_l2), .L1(Game_l1), .S(Game_s), .R1(Game_r1), .R2(Game_r2), .R3(Game_r3));
  Clock Clock (.out(Clock_out));
  LED L3 (.in(Game_l3));
  LED L2 (.in(Game_l2));
  LED L1 (.in(Game_l1));
  LED S (.in(Game_s));
  LED R1 (.in(Game_r1));
  LED R2 (.in(Game_r2));
  button_synchronizer Button_Synchronizer_3 (
    .bi(BR__button_right_out), .Clock(Clock_out), .bo(Button_Synchronizer_3_bo));
  LED R3 (.in(Game_r3));
  Button BR__button_right (.out(BR__button_right_out));
  button_synchronizer Button_Synchronizer_4 (.bi(Game_r3), .Clock(Clock_out), .bo(Button_Synchronizer_4_bo));
  score_board Right_Score_Board (
    .W(Button_Synchronizer_4_bo), .Clock(Clock_out), .Reset(Score_Board_Reset_out),
    .Score(Right_Score_Board_score));
  Hex_Digit_Display hex_digit_display_2 (.value(Right_Score_Board_score));  // open: dp
endmodule

module button_synchronizer (
  input  bi,
  input  Clock,
  output bo
);

  wire and_1_out, and_2_out, not_1_out, not_2_out, not_3_out, not_4_out, not_5_out;
  wire [1:0] and_3_out, register_1_q;

  not not_1 (not_1_out, register_1_q[1]);
  not not_2 (not_2_out, register_1_q[0]);
  not not_3 (not_3_out, register_1_q[1]);
  not not_4 (not_4_out, register_1_q[0]);
  not not_5 (not_5_out, register_1_q[1]);
  and and_1 (and_1_out, not_1_out, register_1_q[0], bi);
  and and_2 (and_2_out, register_1_q[1], not_2_out, bi);
  and and_3 (and_3_out[0], not_3_out, not_4_out, bi);
  and and_4 (bo, not_5_out, register_1_q[0]);
  or or_1 (and_3_out[1], and_1_out, and_2_out);
  Register #(.width(2)) register_1 (.D(and_3_out), .en(1'b1), .Q(register_1_q), .clk(Clock));  // open: clr

  // Notes on the sheet:
  //   s0
  //   s1
  //   n1
  //   n0
endmodule

module Turn_Leds (
  input  BL,
  input  BR,
  input  Reset,
  input  Clock,
  output L3,
  output L2,
  output L1,
  output S,
  output R1,
  output R2,
  output R3
);

  wire and_1_out, and_2_out, and_3_out, and_4_out, and_5_out, and_6_out, and_7_out, and_8_out, and_9_out,
       and_10_out, and_11_out, and_13_out, and_14_out, and_15_out, and_16_out, not_1_out, not_2_out,
       not_3_out, not_4_out, not_5_out, not_6_out, not_7_out, not_8_out, not_9_out, not_10_out, not_11_out,
       not_12_out, not_13_out, not_14_out, not_15_out, not_16_out, not_17_out, not_18_out, not_19_out,
       not_20_out, not_21_out, not_22_out, not_23_out, not_24_out, not_25_out, not_26_out, not_27_out,
       not_28_out, not_29_out, not_30_out, not_31_out;
  wire [2:0] or_3_out, register_1_q;

  not not_1 (not_1_out, register_1_q[1]);
  not not_2 (not_2_out, register_1_q[0]);
  not not_3 (not_3_out, BL);
  not not_4 (not_4_out, register_1_q[1]);
  not not_5 (not_5_out, BR);
  not not_6 (not_6_out, BL);
  not not_7 (not_7_out, BR);
  not not_8 (not_8_out, BR);
  not not_9 (not_9_out, register_1_q[2]);
  not not_10 (not_10_out, register_1_q[0]);
  not not_11 (not_11_out, register_1_q[0]);
  not not_12 (not_12_out, BL);
  not not_13 (not_13_out, BR);
  not not_14 (not_14_out, BL);
  and and_1 (and_1_out, not_1_out, not_2_out, not_3_out, BR);
  and and_2 (and_2_out, not_4_out, register_1_q[0], BL, not_5_out);
  and and_3 (and_3_out, register_1_q[2], not_6_out, not_7_out);
  and and_4 (and_4_out, register_1_q[2], BL, BR);
  and and_5 (and_5_out, register_1_q[2], register_1_q[1], not_8_out);
  and and_6 (and_6_out, register_1_q[2], register_1_q[1], register_1_q[0]);
  and and_7 (and_7_out, not_9_out, register_1_q[1], not_10_out);
  and and_8 (and_8_out, register_1_q[2], not_11_out, not_12_out, BR);
  and and_9 (and_9_out, register_1_q[2], register_1_q[0], BL, not_13_out);
  and and_10 (and_10_out, register_1_q[2], register_1_q[1], not_14_out);
  and and_11 (and_11_out, register_1_q[2], register_1_q[1], BR);
  or or_1 (or_3_out[2], and_1_out, and_2_out, and_3_out, and_4_out, and_5_out, and_6_out);
  or or_2 (or_3_out[1], and_7_out, and_8_out, and_9_out, and_10_out, and_11_out);
  not not_15 (not_15_out, register_1_q[2]);
  not not_16 (not_16_out, register_1_q[1]);
  not not_17 (not_17_out, BR);
  not not_18 (not_18_out, register_1_q[1]);
  not not_19 (not_19_out, BR);
  not not_20 (not_20_out, register_1_q[1]);
  and and_12 (L3, register_1_q[2], register_1_q[1], register_1_q[0]);
  not not_21 (not_21_out, register_1_q[1]);
  not not_22 (not_22_out, register_1_q[2]);
  not not_23 (not_23_out, register_1_q[1]);
  not not_24 (not_24_out, register_1_q[2]);
  not not_25 (not_25_out, register_1_q[1]);
  not not_26 (not_26_out, register_1_q[0]);
  not not_27 (not_27_out, register_1_q[1]);
  not not_28 (not_28_out, register_1_q[0]);
  not not_29 (not_29_out, register_1_q[0]);
  not not_30 (not_30_out, register_1_q[2]);
  not not_31 (not_31_out, register_1_q[0]);
  and and_13 (and_13_out, not_15_out, not_16_out, BL, not_17_out);
  and and_14 (and_14_out, not_18_out, register_1_q[0], not_19_out);
  and and_15 (and_15_out, not_20_out, register_1_q[0], BL);
  and and_16 (and_16_out, register_1_q[2], register_1_q[0]);
  and and_17 (L2, register_1_q[2], not_21_out, register_1_q[0]);
  and and_18 (L1, not_22_out, not_23_out, register_1_q[0]);
  and and_19 (S, not_24_out, not_25_out, not_26_out);
  and and_20 (R1, register_1_q[2], not_27_out, not_28_out);
  and and_21 (R2, register_1_q[2], register_1_q[1], not_29_out);
  and and_22 (R3, not_30_out, register_1_q[1], not_31_out);
  or or_3 (or_3_out[0], and_13_out, and_14_out, and_15_out, and_16_out);
  Register #(.width(3)) register_1 (.D(or_3_out), .en(1'b1), .Q(register_1_q), .clk(Clock), .clr(Reset));

  // Notes on the sheet:
  //   D3
  //   D2
  //   Q3
  //   Q2
  //   Q1
  //   D1
endmodule

module score_board (
  input  Reset,
  input  Clock,
  input  W,
  output [3:0] Score
);

  wire and_1_out, and_2_out, and_3_out, and_4_out, and_5_out, and_6_out, and_7_out, and_8_out, and_9_out,
       and_10_out, and_11_out, and_12_out, and_13_out, not_1_out, not_2_out, not_3_out, not_4_out, not_5_out,
       not_6_out, not_7_out, not_8_out, not_9_out;
  wire [3:0] register_1_q;

  and and_1 (and_1_out, register_1_q[2], register_1_q[1], register_1_q[0], W);
  not not_1 (not_1_out, register_1_q[2]);
  not not_2 (not_2_out, register_1_q[1]);
  not not_3 (not_3_out, register_1_q[0]);
  not not_4 (not_4_out, W);
  not not_5 (not_5_out, register_1_q[1]);
  not not_6 (not_6_out, register_1_q[0]);
  not not_7 (not_7_out, W);
  not not_8 (not_8_out, register_1_q[0]);
  not not_9 (not_9_out, W);
  or or_1 (Score[3], and_1_out, register_1_q[3]);
  and and_2 (and_2_out, not_1_out, register_1_q[1], register_1_q[0], W);
  and and_3 (and_3_out, register_1_q[2], not_2_out);
  and and_4 (and_4_out, register_1_q[2], not_3_out);
  and and_5 (and_5_out, register_1_q[2], not_4_out);
  and and_6 (and_6_out, register_1_q[3], register_1_q[2]);
  and and_7 (and_7_out, not_5_out, register_1_q[0], W);
  and and_8 (and_8_out, register_1_q[1], not_6_out);
  and and_9 (and_9_out, register_1_q[1], not_7_out);
  and and_10 (and_10_out, register_1_q[3], register_1_q[2], register_1_q[1]);
  and and_11 (and_11_out, not_8_out, W);
  and and_12 (and_12_out, register_1_q[0], not_9_out);
  and and_13 (and_13_out, register_1_q[3], register_1_q[2], register_1_q[1], register_1_q[0]);
  or or_2 (Score[2], and_2_out, and_3_out, and_4_out, and_5_out, and_6_out);
  or or_3 (Score[1], and_7_out, and_8_out, and_9_out, and_10_out);
  or or_4 (Score[0], and_11_out, and_12_out, and_13_out);
  Register #(.width(4)) register_1 (.D(Score), .en(1'b1), .Q(register_1_q), .clk(Clock), .clr(Reset));

  // Notes on the sheet:
  //   S3
  //   S2
  //   S1
  //   S0
  //   N3
  //   N2
  //   N1
  //   N0
endmodule
