// Logisim project 1801042004.circ as structural Verilog: 3 circuits, main circuit main
module main (
  input  Start,
  input  [15:0] a_i,
  input  [15:0] b_i
);

  wire clock_1_out, Control_Unit_la, Control_Unit_lb, Control_Unit_lm, Control_Unit_select, Datapath_c;

  Clock clock_1 (.out(clock_1_out));
  control_unit Control_Unit (
    .Start(Start), .C(Datapath_c), .clock(clock_1_out), .la(Control_Unit_la), .lb(Control_Unit_lb),
    .lm(Control_Unit_lm), .Select(Control_Unit_select));
  datapath Datapath (
    .a_i(a_i), .Select(Control_Unit_select), .la(Control_Unit_la), .lb(Control_Unit_lb),
    .lm(Control_Unit_lm), .b_i(b_i), .C(Datapath_c), .clock(clock_1_out));

  // Notes on the sheet:
  //   C
endmodule

module control_unit (
  input  clock,
  input  Start,
  input  C,
  output la,
  output lb,
  output lm,
  output Select
);

  wire and_2_out, and_3_out, and_4_out, and_5_out, and_6_out, and_7_out, not_1_out, not_2_out, not_3_out;
  wire [2:0] or_5_out, states_q;

  not not_1 (not_1_out, states_q[2]);
  not not_2 (not_2_out, states_q[1]);
  not not_3 (not_3_out, states_q[0]);
  and and_1 (lb, states_q[2], not_2_out, states_q[0]);
  and and_2 (and_2_out, not_1_out, not_2_out, not_3_out, Start);
  and and_3 (and_3_out, not_1_out, states_q[1], states_q[0]);
  and and_4 (and_4_out, states_q[1], not_3_out, C);
  and and_5 (and_5_out, states_q[2], not_2_out, states_q[0]);
  and and_6 (and_6_out, states_q[2], states_q[1], not_3_out);
  and and_7 (and_7_out, not_1_out, states_q[1], not_3_out, C);
  or or_1 (la, lb, and_6_out);
  or or_2 (lm, and_3_out, lb);
  and and_8 (Select, states_q[2], not_2_out, states_q[0]);
  or or_3 (or_5_out[2], and_2_out, and_3_out);
  or or_4 (or_5_out[1], and_4_out, and_3_out, and_5_out, and_6_out);
  or or_5 (or_5_out[0], and_2_out, and_7_out);
  Register #(.width(3)) states (.D(or_5_out), .en(1'b1), .Q(states_q), .clk(clock));  // open: clr

  // Notes on the sheet:
  //   s2'
  //   s1'
  //   s0'
  //   s2
  //   s1
  //   s0
  //   n2
  //   n1
  //   n0
  //   s2
  //   s1
  //   s0
endmodule

module datapath (
  input  [15:0] a_i,
  input  Select,
  input  la,
  input  lb,
  input  lm,
  input  [15:0] b_i,
  input  clock,
  output C
);

  wire [15:0] a_q, adder_1_out, b_q, mult_q, multiplexer_1_out, multiplexer_2_out, multiplexer_3_out,
       multiplexer_4_out;

  Multiplexer #(.width(16), .enable("false")) multiplexer_1 (
    .in0(adder_1_out), .in1(a_i), .out(multiplexer_1_out), .sel(Select));
  Register #(.width(16)) a (.D(multiplexer_1_out), .en(la), .Q(a_q), .clk(clock));  // open: clr
  Register #(.width(16)) b (.D(b_i), .en(lb), .Q(b_q), .clk(clock));  // open: clr
  Multiplexer #(.width(16), .enable("false")) multiplexer_2 (
    .in0(mult_q), .in1(a_q), .out(multiplexer_2_out), .sel(la));
  Multiplexer #(.width(16), .enable("false")) multiplexer_3 (
    .in0(b_q), .in1({16{1'b1}}), .out(multiplexer_3_out), .sel(la));
  Comparator #(.width(16)) comparator_1 (.a(a_q), .b({16{1'b0}}), .gt(C));  // open: eq, lt
  Adder #(.width(16)) adder_1 (
    .a(multiplexer_2_out), .b(multiplexer_3_out), .out(adder_1_out), .cin(1'b0));  // open: cout
  Multiplexer #(.width(16), .enable("false")) multiplexer_4 (
    .in0(adder_1_out), .in1({16{1'b0}}), .out(multiplexer_4_out), .sel(Select));
  Register #(.width(16)) mult (.D(multiplexer_4_out), .en(lm), .Q(mult_q), .clk(clock));  // open: clr
endmodule
